// Logisim project Questão 1 FlipFlop D.circ as structural Verilog: 1 circuit, main circuit main
module main (
  input  in_1,
  input  in_2,
  input  in_3,
  output out_4,
  output out_5
);

  wire clock_1_out, nand_1_out, nand_2_out, nand_3_out, nand_4_out, nand_5_out, nand_6_out, not_1_out,
       not_2_out, not_3_out, not_4_out, not_5_out;

  Clock clock_1 (.out(clock_1_out));
  not not_1 (not_1_out, clock_1_out);
  not not_2 (not_2_out, in_2);
  not not_3 (not_3_out, in_1);
  nand nand_1 (nand_1_out, out_5, in_2, not_1_out);
  nand nand_2 (nand_2_out, not_1_out, not_2_out, out_4);
  not not_4 (not_4_out, in_3);
  nand nand_3 (nand_3_out, not_3_out, nand_1_out, nand_4_out);
  not not_5 (not_5_out, not_1_out);
  nand nand_4 (nand_4_out, nand_3_out, nand_2_out, not_4_out);
  nand nand_5 (nand_5_out, nand_3_out, not_4_out, not_5_out);
  nand nand_6 (nand_6_out, not_5_out, not_3_out, nand_4_out);
  nand nand_7 (out_4, not_3_out, out_5, nand_5_out);
  nand nand_8 (out_5, nand_6_out, out_4, not_4_out);
endmodule
