// Logisim project Questão 7 - Banco de Registradores.circ as structural Verilog: 2 circuits, main circuit Banco de Registradores
module Registrador (
  input  SET,
  input  [7:0] in_2,
  input  CLOCK,
  input  RESET,
  output [7:0] out_5
);

  wire nand_1_out, nand_2_out, nand_3_out, nand_4_out, nand_5_out, nand_6_out, nand_7_out, nand_8_out,
       nand_9_out, nand_10_out, nand_11_out, nand_12_out, nand_13_out, nand_14_out, nand_15_out, nand_16_out,
       nand_17_out, nand_18_out, nand_19_out, nand_20_out, nand_21_out, nand_22_out, nand_23_out,
       nand_24_out, nand_25_out, nand_26_out, nand_27_out, nand_28_out, nand_29_out, nand_30_out,
       nand_31_out, nand_32_out, nand_33_out, nand_34_out, nand_35_out, nand_36_out, nand_37_out,
       nand_38_out, nand_39_out, nand_40_out, nand_41_out, nand_42_out, nand_43_out, nand_44_out,
       nand_45_out, nand_46_out, nand_47_out, nand_48_out, nand_50_out, nand_52_out, nand_54_out,
       nand_56_out, nand_58_out, nand_60_out, nand_62_out, nand_64_out, not_1_out, not_2_out, not_3_out,
       not_4_out, not_5_out, not_6_out, not_7_out, not_8_out, not_9_out, not_10_out, not_11_out, not_12_out,
       not_13_out, not_14_out, not_15_out, not_16_out, not_17_out, not_18_out, not_19_out, not_20_out,
       not_21_out, not_22_out, not_23_out, not_24_out, not_25_out, not_26_out;

  not not_1 (not_1_out, SET);
  not not_2 (not_2_out, RESET);
  not not_3 (not_3_out, CLOCK);
  not not_4 (not_4_out, CLOCK);
  not not_5 (not_5_out, CLOCK);
  not not_6 (not_6_out, CLOCK);
  not not_7 (not_7_out, in_2[0]);
  not not_8 (not_8_out, in_2[1]);
  not not_9 (not_9_out, in_2[2]);
  not not_10 (not_10_out, in_2[3]);
  not not_11 (not_11_out, CLOCK);
  not not_12 (not_12_out, in_2[4]);
  not not_13 (not_13_out, CLOCK);
  not not_14 (not_14_out, in_2[5]);
  not not_15 (not_15_out, CLOCK);
  not not_16 (not_16_out, in_2[6]);
  not not_17 (not_17_out, CLOCK);
  not not_18 (not_18_out, in_2[7]);
  nand nand_1 (nand_1_out, nand_50_out, in_2[0], not_3_out);
  nand nand_2 (nand_2_out, not_3_out, not_7_out, out_5[0]);
  nand nand_3 (nand_3_out, nand_52_out, in_2[1], not_4_out);
  nand nand_4 (nand_4_out, not_4_out, not_8_out, out_5[1]);
  nand nand_5 (nand_5_out, nand_54_out, in_2[2], not_5_out);
  nand nand_6 (nand_6_out, not_5_out, not_9_out, out_5[2]);
  nand nand_7 (nand_7_out, nand_56_out, in_2[3], not_6_out);
  nand nand_8 (nand_8_out, not_6_out, not_10_out, out_5[3]);
  nand nand_9 (nand_9_out, nand_58_out, in_2[4], not_11_out);
  nand nand_10 (nand_10_out, not_11_out, not_12_out, out_5[4]);
  nand nand_11 (nand_11_out, nand_60_out, in_2[5], not_13_out);
  nand nand_12 (nand_12_out, not_13_out, not_14_out, out_5[5]);
  nand nand_13 (nand_13_out, nand_62_out, in_2[6], not_15_out);
  nand nand_14 (nand_14_out, not_15_out, not_16_out, out_5[6]);
  nand nand_15 (nand_15_out, nand_64_out, in_2[7], not_17_out);
  nand nand_16 (nand_16_out, not_17_out, not_18_out, out_5[7]);
  nand nand_17 (nand_17_out, not_1_out, nand_1_out, nand_18_out);
  nand nand_18 (nand_18_out, nand_17_out, nand_2_out, not_2_out);
  nand nand_19 (nand_19_out, not_1_out, nand_3_out, nand_20_out);
  nand nand_20 (nand_20_out, nand_19_out, nand_4_out, not_2_out);
  nand nand_21 (nand_21_out, not_1_out, nand_5_out, nand_22_out);
  nand nand_22 (nand_22_out, nand_21_out, nand_6_out, not_2_out);
  nand nand_23 (nand_23_out, not_1_out, nand_7_out, nand_24_out);
  nand nand_24 (nand_24_out, nand_23_out, nand_8_out, not_2_out);
  nand nand_25 (nand_25_out, not_1_out, nand_9_out, nand_26_out);
  nand nand_26 (nand_26_out, nand_25_out, nand_10_out, not_2_out);
  nand nand_27 (nand_27_out, not_1_out, nand_11_out, nand_28_out);
  nand nand_28 (nand_28_out, nand_27_out, nand_12_out, not_2_out);
  nand nand_29 (nand_29_out, not_1_out, nand_13_out, nand_30_out);
  nand nand_30 (nand_30_out, nand_29_out, nand_14_out, not_2_out);
  nand nand_31 (nand_31_out, not_1_out, nand_15_out, nand_32_out);
  nand nand_32 (nand_32_out, nand_31_out, nand_16_out, not_2_out);
  not not_19 (not_19_out, not_3_out);
  not not_20 (not_20_out, not_4_out);
  not not_21 (not_21_out, not_5_out);
  not not_22 (not_22_out, not_6_out);
  not not_23 (not_23_out, not_11_out);
  not not_24 (not_24_out, not_13_out);
  not not_25 (not_25_out, not_15_out);
  not not_26 (not_26_out, not_17_out);
  nand nand_33 (nand_33_out, nand_17_out, not_2_out, not_19_out);
  nand nand_34 (nand_34_out, not_19_out, not_1_out, nand_18_out);
  nand nand_35 (nand_35_out, nand_19_out, not_2_out, not_20_out);
  nand nand_36 (nand_36_out, not_20_out, not_1_out, nand_20_out);
  nand nand_37 (nand_37_out, nand_21_out, not_2_out, not_21_out);
  nand nand_38 (nand_38_out, not_21_out, not_1_out, nand_22_out);
  nand nand_39 (nand_39_out, nand_23_out, not_2_out, not_22_out);
  nand nand_40 (nand_40_out, not_22_out, not_1_out, nand_24_out);
  nand nand_41 (nand_41_out, nand_25_out, not_2_out, not_23_out);
  nand nand_42 (nand_42_out, not_23_out, not_1_out, nand_26_out);
  nand nand_43 (nand_43_out, nand_27_out, not_2_out, not_24_out);
  nand nand_44 (nand_44_out, not_24_out, not_1_out, nand_28_out);
  nand nand_45 (nand_45_out, nand_29_out, not_2_out, not_25_out);
  nand nand_46 (nand_46_out, not_25_out, not_1_out, nand_30_out);
  nand nand_47 (nand_47_out, nand_31_out, not_2_out, not_26_out);
  nand nand_48 (nand_48_out, not_26_out, not_1_out, nand_32_out);
  nand nand_49 (out_5[0], not_1_out, nand_50_out, nand_33_out);
  nand nand_50 (nand_50_out, nand_34_out, out_5[0], not_2_out);
  nand nand_51 (out_5[1], not_1_out, nand_52_out, nand_35_out);
  nand nand_52 (nand_52_out, nand_36_out, out_5[1], not_2_out);
  nand nand_53 (out_5[2], not_1_out, nand_54_out, nand_37_out);
  nand nand_54 (nand_54_out, nand_38_out, out_5[2], not_2_out);
  nand nand_55 (out_5[3], not_1_out, nand_56_out, nand_39_out);
  nand nand_56 (nand_56_out, nand_40_out, out_5[3], not_2_out);
  nand nand_57 (out_5[4], not_1_out, nand_58_out, nand_41_out);
  nand nand_58 (nand_58_out, nand_42_out, out_5[4], not_2_out);
  nand nand_59 (out_5[5], not_1_out, nand_60_out, nand_43_out);
  nand nand_60 (nand_60_out, nand_44_out, out_5[5], not_2_out);
  nand nand_61 (out_5[6], not_1_out, nand_62_out, nand_45_out);
  nand nand_62 (nand_62_out, nand_46_out, out_5[6], not_2_out);
  nand nand_63 (out_5[7], not_1_out, nand_64_out, nand_47_out);
  nand nand_64 (nand_64_out, nand_48_out, out_5[7], not_2_out);
endmodule

module Banco_de_Registradores (
  input  RESET,
  input  [7:0] INPUT,
  input  SET,
  input  [1:0] \ENDEREÇO ,
  output [7:0] out_5,
  output [7:0] out_6,
  output [7:0] out_7,
  output [7:0] out_8
);

  wire CLOCK_out, demultiplexer_1_out0, demultiplexer_1_out1, demultiplexer_1_out2, demultiplexer_1_out3;

  Clock CLOCK (.out(CLOCK_out));
  Demultiplexer #(.select(2)) demultiplexer_1 (
    .out0(demultiplexer_1_out0), .out1(demultiplexer_1_out1), .out2(demultiplexer_1_out2),
    .out3(demultiplexer_1_out3), .in(CLOCK_out), .sel(\ENDEREÇO ));  // open: en
  Registrador registrador_1 (.SET(SET), .CLOCK(demultiplexer_1_out0), .RESET(RESET), .in_2(INPUT), .out_5(out_5));
  Registrador registrador_2 (.SET(SET), .CLOCK(demultiplexer_1_out1), .RESET(RESET), .in_2(INPUT), .out_5(out_6));
  Registrador registrador_3 (.SET(SET), .CLOCK(demultiplexer_1_out2), .RESET(RESET), .in_2(INPUT), .out_5(out_7));
  Registrador registrador_4 (.SET(SET), .CLOCK(demultiplexer_1_out3), .RESET(RESET), .in_2(INPUT), .out_5(out_8));
endmodule
