// Logisim project Questão 1 FlipFlop D.circ as structural Verilog: 1 circuit, main circuit main
module main (
  input  SET,
  input  D,
  input  RESET,
  output Q,
  output nQ
);

  wire CLOCK_out, nand_1_out, nand_2_out, nand_3_out, nand_4_out, nand_5_out, nand_6_out, not_1_out,
       not_2_out, not_3_out, not_4_out, not_5_out;

  Clock CLOCK (.out(CLOCK_out));
  not not_1 (not_1_out, D);
  not not_2 (not_2_out, CLOCK_out);
  not not_3 (not_3_out, SET);
  nand nand_1 (nand_1_out, nQ, D, not_2_out);
  nand nand_2 (nand_2_out, not_2_out, not_1_out, Q);
  not not_4 (not_4_out, RESET);
  nand nand_3 (nand_3_out, not_3_out, nand_1_out, nand_4_out);
  not not_5 (not_5_out, not_2_out);
  nand nand_4 (nand_4_out, nand_3_out, nand_2_out, not_4_out);
  nand nand_5 (nand_5_out, nand_3_out, not_4_out, not_5_out);
  nand nand_6 (nand_6_out, not_5_out, not_3_out, nand_4_out);
  nand nand_7 (Q, not_3_out, nQ, nand_5_out);
  nand nand_8 (nQ, nand_6_out, Q, not_4_out);

  // Notes on the sheet:
  //   D
  //   ~D
endmodule
