// Logisim project Questão 10 - ULA 8 bits.circ as structural Verilog: 2 circuits, main circuit ULA 8 bits - Main
module ULA___Controle (
  input  [1:0] A_B,
  input  [1:0] SA_SB,
  input  Cin,
  input  [2:0] SELETOR,
  input  CinShiftE,
  input  CinShiftD,
  output S,
  output Cout,
  output CoutShiftE,
  output CoutShiftD
);

  wire adder_1_cout, adder_1_out, and_1_out, and_2_out, and_3_out, and_4_out, and_5_out, and_6_out,
       and_7_out, and_8_out, and_9_out, and_10_out, and_11_out, and_12_out, and_13_out, and_15_out,
       not_1_out, not_2_out, not_3_out, not_4_out, not_5_out, not_6_out, not_7_out, not_8_out, not_9_out,
       not_10_out, not_11_out, not_12_out, not_13_out, not_14_out, not_15_out, not_16_out, not_17_out,
       not_18_out, not_19_out, not_20_out, not_21_out, or_1_out, or_2_out, or_3_out, subtractor_1_bout,
       subtractor_1_out, xor_1_out;

  // Probe on A_B[0]
  // Probe on A_B[1]
  not not_1 (not_1_out, SA_SB[0]);
  not not_2 (not_2_out, A_B[0]);
  not not_3 (not_3_out, SA_SB[1]);
  not not_4 (not_4_out, A_B[1]);
  and and_1 (and_1_out, not_1_out, A_B[0]);
  and and_2 (and_2_out, SA_SB[0], not_2_out);
  and and_3 (and_3_out, not_3_out, A_B[1]);
  and and_4 (and_4_out, SA_SB[1], not_4_out);
  or or_1 (or_1_out, and_1_out, and_2_out);
  or or_2 (or_2_out, and_3_out, and_4_out);
  and and_5 (and_5_out, or_1_out, or_2_out);
  or or_3 (or_3_out, or_1_out, or_2_out);
  xor xor_1 (xor_1_out, or_1_out, or_2_out);
  Adder #(.width(1)) adder_1 (.a(or_1_out), .b(or_2_out), .out(adder_1_out), .cin(Cin), .cout(adder_1_cout));
  Subtractor #(.width(1)) subtractor_1 (
    .a(or_1_out), .b(or_2_out), .out(subtractor_1_out), .bin(Cin), .bout(subtractor_1_bout));
  not not_5 (not_5_out, SELETOR[2]);
  not not_6 (not_6_out, SELETOR[2]);
  not not_7 (not_7_out, SELETOR[0]);
  not not_8 (not_8_out, SELETOR[1]);
  not not_9 (not_9_out, SELETOR[0]);
  not not_10 (not_10_out, SELETOR[1]);
  not not_11 (not_11_out, SELETOR[1]);
  not not_12 (not_12_out, SELETOR[1]);
  not not_13 (not_13_out, SELETOR[0]);
  not not_14 (not_14_out, SELETOR[0]);
  not not_15 (not_15_out, SELETOR[0]);
  not not_16 (not_16_out, SELETOR[1]);
  and and_6 (and_6_out, not_15_out, not_16_out, not_17_out, and_5_out);
  not not_17 (not_17_out, SELETOR[2]);
  not not_18 (not_18_out, SELETOR[1]);
  and and_7 (and_7_out, SELETOR[0], not_18_out, not_19_out, or_3_out);
  not not_19 (not_19_out, SELETOR[2]);
  not not_20 (not_20_out, SELETOR[0]);
  and and_8 (and_8_out, not_20_out, SELETOR[1], not_21_out, xor_1_out);
  not not_21 (not_21_out, SELETOR[2]);
  and and_9 (and_9_out, SELETOR[0], SELETOR[1], not_5_out, adder_1_out);
  and and_10 (and_10_out, SELETOR[0], SELETOR[1], not_6_out, adder_1_cout);
  and and_11 (and_11_out, not_7_out, not_8_out, SELETOR[2], subtractor_1_out);
  and and_12 (and_12_out, not_9_out, not_10_out, SELETOR[2], subtractor_1_bout);
  and and_13 (and_13_out, SELETOR[0], not_11_out, SELETOR[2], CinShiftE);
  and and_14 (CoutShiftE, SELETOR[0], not_12_out, SELETOR[2], A_B[0]);
  and and_15 (and_15_out, not_13_out, SELETOR[1], SELETOR[2], CinShiftD);
  and and_16 (CoutShiftD, not_14_out, SELETOR[1], SELETOR[2], A_B[0]);
  or or_4 (S, and_6_out, and_7_out, and_8_out, and_9_out, and_11_out, and_13_out, and_15_out);
  or or_5 (Cout, and_10_out, and_12_out);

  // Notes on the sheet:
  //   0
  //   1
  //   0
  //   1
  //   000
  //   001
  //   010
  //   011
  //   011
  //   100
  //   100
  //   101
  //   101
  //   110
  //   110
endmodule

module ULA_8_bits___Main (
  input  [4:0] SELETOR,
  input  [7:0] A,
  input  [7:0] B,
  output OVERFLOW,
  output [7:0] S
);

  wire ula_controle_1_cout, ula_controle_1_coutshifte, ula_controle_2_cout, ula_controle_2_coutshifte,
       ula_controle_3_cout, ula_controle_3_coutshiftd, ula_controle_3_coutshifte, ula_controle_4_cout,
       ula_controle_4_coutshiftd, ula_controle_4_coutshifte, ula_controle_5_cout, ula_controle_5_coutshiftd,
       ula_controle_5_coutshifte, ula_controle_6_cout, ula_controle_6_coutshiftd, ula_controle_6_coutshifte,
       ula_controle_7_cout, ula_controle_7_coutshiftd, ula_controle_8_coutshiftd;

  ULA___Controle ula_controle_1 (
    .S(S[0]), .Cout(ula_controle_1_cout), .A_B({B[0], A[0]}), .SA_SB({SELETOR[3], SELETOR[4]}), .Cin(1'b0),
    .SELETOR(SELETOR[2:0]), .CoutShiftE(ula_controle_1_coutshifte), .CinShiftE(1'b0),
    .CinShiftD(ula_controle_3_coutshiftd));  // open: CoutShiftD
  ULA___Controle ula_controle_2 (
    .S(S[1]), .Cout(ula_controle_2_cout), .A_B({B[1], A[1]}), .SA_SB({SELETOR[3], SELETOR[4]}),
    .Cin(ula_controle_1_cout), .SELETOR(SELETOR[2:0]), .CoutShiftE(ula_controle_2_coutshifte),
    .CinShiftE(1'b0), .CinShiftD(ula_controle_4_coutshiftd));  // open: CoutShiftD
  ULA___Controle ula_controle_3 (
    .S(S[2]), .Cout(ula_controle_3_cout), .A_B({B[2], A[2]}), .SA_SB({SELETOR[3], SELETOR[4]}),
    .Cin(ula_controle_2_cout), .SELETOR(SELETOR[2:0]), .CoutShiftE(ula_controle_3_coutshifte),
    .CinShiftE(ula_controle_1_coutshifte), .CinShiftD(ula_controle_5_coutshiftd),
    .CoutShiftD(ula_controle_3_coutshiftd));
  ULA___Controle ula_controle_4 (
    .S(S[3]), .Cout(ula_controle_4_cout), .A_B({B[3], A[3]}), .SA_SB({SELETOR[3], SELETOR[4]}),
    .Cin(ula_controle_3_cout), .SELETOR(SELETOR[2:0]), .CoutShiftE(ula_controle_4_coutshifte),
    .CinShiftE(ula_controle_2_coutshifte), .CinShiftD(ula_controle_6_coutshiftd),
    .CoutShiftD(ula_controle_4_coutshiftd));
  ULA___Controle ula_controle_5 (
    .S(S[4]), .Cout(ula_controle_5_cout), .A_B({B[4], A[4]}), .SA_SB({SELETOR[3], SELETOR[4]}),
    .Cin(ula_controle_4_cout), .SELETOR(SELETOR[2:0]), .CoutShiftE(ula_controle_5_coutshifte),
    .CinShiftE(ula_controle_3_coutshifte), .CinShiftD(ula_controle_7_coutshiftd),
    .CoutShiftD(ula_controle_5_coutshiftd));
  ULA___Controle ula_controle_6 (
    .S(S[5]), .Cout(ula_controle_6_cout), .A_B({B[5], A[5]}), .SA_SB({SELETOR[3], SELETOR[4]}),
    .Cin(ula_controle_5_cout), .SELETOR(SELETOR[2:0]), .CoutShiftE(ula_controle_6_coutshifte),
    .CinShiftE(ula_controle_4_coutshifte), .CinShiftD(ula_controle_8_coutshiftd),
    .CoutShiftD(ula_controle_6_coutshiftd));
  ULA___Controle ula_controle_7 (
    .S(S[6]), .Cout(ula_controle_7_cout), .A_B({B[6], A[6]}), .SA_SB({SELETOR[3], SELETOR[4]}),
    .Cin(ula_controle_6_cout), .SELETOR(SELETOR[2:0]), .CinShiftE(ula_controle_5_coutshifte),
    .CinShiftD(1'b0), .CoutShiftD(ula_controle_7_coutshiftd));  // open: CoutShiftE
  ULA___Controle ula_controle_8 (
    .S(S[7]), .Cout(OVERFLOW), .A_B({B[7], A[7]}), .SA_SB({SELETOR[3], SELETOR[4]}),
    .Cin(ula_controle_7_cout), .SELETOR(SELETOR[2:0]), .CinShiftE(ula_controle_6_coutshifte),
    .CinShiftD(1'b0), .CoutShiftD(ula_controle_8_coutshiftd));  // open: CoutShiftE

  // Notes on the sheet:
  //   00000: E
  //   00001: OU
  //   00010: XOR
  //   11001: NÃO E
  //   11000: NÃO OU
  //   10011: NÂO
  //   00011: SOMA
  //   00100: SUB
  //   00101: SHIF E. 
  //   00110: SHIF D.
endmodule
