// Logisim project Questão 11 - Extensor de Sinal.circ as structural Verilog: 1 circuit, main circuit main
module main (
  input  [3:0] INPUTS,
  input  \Tipo_de_Extensão ,
  output [7:0] Sinal_Final
);


  assign Sinal_Final = {{4{\Tipo_de_Extensão }}, INPUTS};
endmodule
