// Logisim project Questão 12 - Máquina de Estados Hebert.circ as structural Verilog: 2 circuits, main circuit main
module main (
  input  SET,
  input  RESET,
  input  P,
  output R
);

  wire and_1_out, and_2_out, and_3_out, and_4_out, and_5_out, and_6_out, and_7_out, and_8_out, and_9_out,
       clock_1_out, ff_d_1_q, ff_d_2_q, ff_d_3_q, not_1_out, not_2_out, not_3_out, not_4_out, not_5_out,
       not_6_out, not_7_out, or_1_out, or_2_out, or_3_out;

  Clock clock_1 (.out(clock_1_out));
  and and_1 (and_1_out, not_1_out, R);
  and and_2 (and_2_out, not_1_out, ff_d_1_q);
  and and_3 (and_3_out, not_2_out, not_3_out, not_4_out, not_5_out);
  or or_1 (or_1_out, and_3_out, and_2_out, and_1_out);
  LED A (.in(ff_d_1_q));
  not not_1 (not_1_out, P);
  not not_2 (not_2_out, R);
  not not_3 (not_3_out, ff_d_3_q);
  not not_4 (not_4_out, ff_d_2_q);
  not not_5 (not_5_out, ff_d_1_q);
  FF_D ff_d_1 (.INPUT(or_1_out), .CLOCK(clock_1_out), .SET(SET), .RESET(RESET), .Q(ff_d_1_q));  // open: nQ
  LED D (.in(R));
  LED C (.in(ff_d_3_q));
  LED B (.in(ff_d_2_q));
  and and_4 (and_4_out, P, R);
  and and_5 (and_5_out, not_6_out, ff_d_2_q);
  and and_6 (and_6_out, P, ff_d_1_q);
  not not_6 (not_6_out, P);
  or or_2 (or_2_out, and_5_out, and_4_out, and_6_out);
  FF_D ff_d_2 (.INPUT(or_2_out), .CLOCK(clock_1_out), .SET(SET), .RESET(RESET), .Q(ff_d_2_q));  // open: nQ
  and and_7 (and_7_out, not_7_out, ff_d_3_q);
  and and_8 (and_8_out, P, ff_d_2_q);
  not not_7 (not_7_out, P);
  or or_3 (or_3_out, and_7_out, and_8_out);
  FF_D ff_d_3 (.INPUT(or_3_out), .CLOCK(clock_1_out), .SET(SET), .RESET(RESET), .Q(ff_d_3_q));  // open: nQ
  and and_9 (and_9_out, P, ff_d_3_q);
  FF_D ff_d_4 (.INPUT(and_9_out), .CLOCK(clock_1_out), .SET(SET), .RESET(RESET), .Q(R));  // open: nQ

  // Notes on the sheet:
  //   A
  //   B
  //   C
  //   D
endmodule

module FF_D (
  input  SET,
  input  INPUT,
  input  CLOCK,
  input  RESET,
  output Q,
  output nQ
);

  wire nand_1_out, nand_2_out, nand_3_out, nand_4_out, nand_5_out, nand_6_out, not_1_out, not_2_out,
       not_3_out, not_4_out;

  not not_1 (not_1_out, INPUT);
  not not_2 (not_2_out, SET);
  nand nand_1 (nand_1_out, nQ, INPUT, CLOCK);
  nand nand_2 (nand_2_out, CLOCK, not_1_out, Q);
  not not_3 (not_3_out, RESET);
  nand nand_3 (nand_3_out, not_2_out, nand_1_out, nand_4_out);
  not not_4 (not_4_out, CLOCK);
  nand nand_4 (nand_4_out, nand_3_out, nand_2_out, not_3_out);
  nand nand_5 (nand_5_out, nand_3_out, not_3_out, not_4_out);
  nand nand_6 (nand_6_out, not_4_out, not_2_out, nand_4_out);
  nand nand_7 (Q, not_2_out, nand_5_out, nQ);
  nand nand_8 (nQ, Q, nand_6_out, not_3_out);
endmodule
