// Logisim project Questão 13 - Contador Síncrono.circ as structural Verilog: 2 circuits, main circuit Main
module Main (
  input  SET,
  input  RESET,
  output out_3,
  output out_4,
  output out_5,
  output out_6
);

  wire and_1_out, and_2_out, clock_1_out;

  and and_1 (and_1_out, and_2_out, out_4);
  FF_T ff_t_1 (.INPUT(and_1_out), .CLOCK(clock_1_out), .Q(out_3), .SET(SET), .RESET(RESET));  // open: nQ
  Clock clock_1 (.out(clock_1_out));
  and and_2 (and_2_out, out_6, out_5);
  FF_T ff_t_2 (.INPUT(and_2_out), .CLOCK(clock_1_out), .Q(out_4), .SET(SET), .RESET(RESET));  // open: nQ
  FF_T ff_t_3 (.INPUT(out_6), .CLOCK(clock_1_out), .Q(out_5), .SET(SET), .RESET(RESET));  // open: nQ
  FF_T ff_t_4 (.INPUT(1'b1), .CLOCK(clock_1_out), .Q(out_6), .SET(SET), .RESET(RESET));  // open: nQ
endmodule

module FF_T (
  input  SET,
  input  INPUT,
  input  CLOCK,
  input  RESET,
  output Q,
  output nQ
);

  wire nand_1_out, nand_2_out, nand_3_out, nand_4_out, nand_5_out, nand_6_out, not_1_out, not_2_out,
       not_3_out, not_4_out;

  not not_1 (not_1_out, CLOCK);
  not not_2 (not_2_out, SET);
  nand nand_1 (nand_1_out, nQ, INPUT, not_1_out);
  nand nand_2 (nand_2_out, not_1_out, INPUT, Q);
  not not_3 (not_3_out, RESET);
  nand nand_3 (nand_3_out, not_2_out, nand_1_out, nand_4_out);
  not not_4 (not_4_out, not_1_out);
  nand nand_4 (nand_4_out, nand_3_out, nand_2_out, not_3_out);
  nand nand_5 (nand_5_out, nand_3_out, not_3_out, not_4_out);
  nand nand_6 (nand_6_out, not_4_out, not_2_out, nand_4_out);
  nand nand_7 (Q, not_2_out, nand_5_out, nQ);
  nand nand_8 (nQ, Q, nand_6_out, not_3_out);
endmodule
