// Logisim project Questão 4 - Somador.circ as structural Verilog: 2 circuits, main circuit main
// S
module main (
  input  in_1,
  input  in_2,
  input  in_3,
  input  _4_plus,
  input  in_5,
  input  in_6,
  input  in_7,
  input  in_8,
  output out_9,
  output out_10,
  output out_11,
  output out_12,
  output out_13,
  output out_14,
  output out_15,
  output out_16,
  output out_17
);

  wire and_1_out, and_2_out, and_3_out, and_4_out, and_5_out, and_6_out, and_7_out, and_8_out, and_9_out,
       and_10_out, and_11_out, and_12_out, and_13_out, and_14_out, and_15_out, and_16_out, and_17_out,
       and_18_out, and_19_out, and_20_out, and_21_out, and_22_out, or_1_out, or_2_out, or_3_out, or_4_out,
       or_5_out, or_6_out, xor_1_out, xor_3_out, xor_5_out, xor_7_out, xor_9_out, xor_11_out, xor_13_out,
       xor_15_out;

  xor xor_1 (xor_1_out, in_8, 1'b0);
  and and_1 (and_1_out, in_8, 1'b0);
  xor xor_2 (out_17, xor_1_out, 1'b0);
  and and_2 (and_2_out, 1'b0, in_7);
  and and_3 (and_3_out, 1'b0, and_1_out);
  and and_4 (and_4_out, in_7, and_1_out);
  xor xor_3 (xor_3_out, in_7, 1'b0);
  or or_1 (or_1_out, and_2_out, and_3_out, and_4_out);
  xor xor_4 (out_16, xor_3_out, and_1_out);
  and and_5 (and_5_out, 1'b1, in_6);
  and and_6 (and_6_out, 1'b1, or_1_out);
  and and_7 (and_7_out, in_6, or_1_out);
  xor xor_5 (xor_5_out, in_6, 1'b1);
  xor xor_6 (out_15, xor_5_out, or_1_out);
  or or_2 (or_2_out, and_5_out, and_6_out, and_7_out);
  xor xor_7 (xor_7_out, in_5, 1'b0);
  and and_8 (and_8_out, 1'b0, in_5);
  and and_9 (and_9_out, 1'b0, or_2_out);
  and and_10 (and_10_out, in_5, or_2_out);
  or or_3 (or_3_out, and_8_out, and_9_out, and_10_out);
  xor xor_8 (out_14, xor_7_out, or_2_out);
  xor xor_9 (xor_9_out, _4_plus, 1'b0);
  and and_11 (and_11_out, 1'b0, _4_plus);
  and and_12 (and_12_out, 1'b0, or_3_out);
  and and_13 (and_13_out, _4_plus, or_3_out);
  or or_4 (or_4_out, and_11_out, and_12_out, and_13_out);
  xor xor_10 (out_13, xor_9_out, or_3_out);
  and and_14 (and_14_out, 1'b0, in_3);
  and and_15 (and_15_out, 1'b0, or_4_out);
  and and_16 (and_16_out, in_3, or_4_out);
  xor xor_11 (xor_11_out, in_3, 1'b0);
  or or_5 (or_5_out, and_14_out, and_15_out, and_16_out);
  xor xor_12 (out_12, xor_11_out, or_4_out);
  and and_17 (and_17_out, 1'b0, in_2);
  and and_18 (and_18_out, 1'b0, or_5_out);
  and and_19 (and_19_out, in_2, or_5_out);
  xor xor_13 (xor_13_out, in_2, 1'b0);
  or or_6 (or_6_out, and_17_out, and_18_out, and_19_out);
  xor xor_14 (out_11, xor_13_out, or_5_out);
  and and_20 (and_20_out, 1'b0, in_1);
  and and_21 (and_21_out, 1'b0, or_6_out);
  and and_22 (and_22_out, in_1, or_6_out);
  xor xor_15 (xor_15_out, in_1, 1'b0);
  or or_7 (out_9, and_20_out, and_21_out, and_22_out);
  xor xor_16 (out_10, xor_15_out, or_6_out);

  // Notes on the sheet:
  //   (4)
endmodule

module \Secção_Somador  (
  input  Cin,
  input  A,
  input  B,
  output S,
  output Cout
);

  wire and_1_out, and_2_out, and_3_out, xor_1_out;

  xor xor_1 (xor_1_out, B, A);
  and and_1 (and_1_out, A, B);
  and and_2 (and_2_out, A, Cin);
  and and_3 (and_3_out, B, Cin);
  xor xor_2 (S, xor_1_out, Cin);
  or or_1 (Cout, and_1_out, and_2_out, and_3_out);

  // Notes on the sheet:
  //   Grupo de E
  //   XOR 1
  //   XOR 2
endmodule
