// Logisim project Questão 5 - Memoria ROM.circ as structural Verilog: 2 circuits, main circuit Memoria ROM
module Valor_de_Memoria (
  input  CLOCK,
  input  [7:0] INPUT,
  input  SET,
  input  RESET,
  output [7:0] OUTPUT
);

  D_Flip_Flop d_ff_1 (.clk(CLOCK), .D(INPUT[0]), .Q(OUTPUT[0]), .preset(SET), .reset(RESET));  // open: Qn, en
  D_Flip_Flop d_ff_2 (.clk(CLOCK), .D(INPUT[1]), .Q(OUTPUT[1]), .preset(SET), .reset(RESET));  // open: Qn, en
  D_Flip_Flop d_ff_3 (.clk(CLOCK), .D(INPUT[2]), .Q(OUTPUT[2]), .preset(SET), .reset(RESET));  // open: Qn, en
  D_Flip_Flop d_ff_4 (.clk(CLOCK), .D(INPUT[3]), .Q(OUTPUT[3]), .preset(SET), .reset(RESET));  // open: Qn, en
  D_Flip_Flop d_ff_5 (.clk(CLOCK), .D(INPUT[4]), .Q(OUTPUT[4]), .preset(SET), .reset(RESET));  // open: Qn, en
  D_Flip_Flop d_ff_6 (.clk(CLOCK), .D(INPUT[5]), .Q(OUTPUT[5]), .preset(SET), .reset(RESET));  // open: Qn, en
  D_Flip_Flop d_ff_7 (.clk(CLOCK), .D(INPUT[6]), .Q(OUTPUT[6]), .preset(SET), .reset(RESET));  // open: Qn, en
  D_Flip_Flop d_ff_8 (.clk(CLOCK), .D(INPUT[7]), .Q(OUTPUT[7]), .preset(SET), .reset(RESET));  // open: Qn, en
endmodule

module Memoria_ROM (
  input  RESET,
  input  ESC_0_LER_1,
  input  SET,
  input  [7:0] INPUT,
  output [7:0] OUTPUT
);

  wire CLOCK_out, demultiplexer_1_out0, demultiplexer_1_out1, demultiplexer_1_out2, demultiplexer_1_out3,
       demultiplexer_1_out4, demultiplexer_1_out5, demultiplexer_1_out6, demultiplexer_1_out7,
       demultiplexer_1_out8, demultiplexer_1_out9, demultiplexer_1_out10, demultiplexer_1_out11,
       demultiplexer_1_out12, demultiplexer_1_out13, demultiplexer_1_out14, demultiplexer_1_out15,
       multiplexer_1_out;
  wire [3:0] counter_1_q, subtractor_1_out;
  wire [7:0] multiplexer_2_out, valor_de_memoria_1_output, valor_de_memoria_2_output,
       valor_de_memoria_3_output, valor_de_memoria_4_output, valor_de_memoria_5_output,
       valor_de_memoria_6_output, valor_de_memoria_7_output, valor_de_memoria_8_output,
       valor_de_memoria_9_output, valor_de_memoria_10_output, valor_de_memoria_11_output,
       valor_de_memoria_12_output, valor_de_memoria_13_output, valor_de_memoria_14_output,
       valor_de_memoria_15_output, valor_de_memoria_16_output;

  Clock CLOCK (.out(CLOCK_out));
  Counter #(.width(4), .max('hf)) counter_1 (
    .count(1'b1), .Q(counter_1_q), .clk(multiplexer_1_out), .clr(RESET));  // open: load, D, carry
  Multiplexer multiplexer_1 (.in0(CLOCK_out), .in1(1'b0), .out(multiplexer_1_out), .sel(ESC_0_LER_1));  // open: en
  Demultiplexer #(.select(4)) demultiplexer_1 (
    .out0(demultiplexer_1_out0), .out1(demultiplexer_1_out1), .out2(demultiplexer_1_out2),
    .out3(demultiplexer_1_out3), .out4(demultiplexer_1_out4), .out5(demultiplexer_1_out5),
    .out6(demultiplexer_1_out6), .out7(demultiplexer_1_out7), .out8(demultiplexer_1_out8),
    .out9(demultiplexer_1_out9), .out10(demultiplexer_1_out10), .out11(demultiplexer_1_out11),
    .out12(demultiplexer_1_out12), .out13(demultiplexer_1_out13), .out14(demultiplexer_1_out14),
    .out15(demultiplexer_1_out15), .in(1'b1), .sel(counter_1_q));  // open: en
  Subtractor #(.width(4)) subtractor_1 (.a(counter_1_q), .b(4'b0001), .out(subtractor_1_out));  // open: bin, bout
  Valor_de_Memoria valor_de_memoria_1 (
    .INPUT(INPUT), .SET(SET), .CLOCK(demultiplexer_1_out0), .RESET(RESET), .OUTPUT(valor_de_memoria_1_output));
  Valor_de_Memoria valor_de_memoria_2 (
    .INPUT(INPUT), .SET(SET), .CLOCK(demultiplexer_1_out1), .RESET(RESET), .OUTPUT(valor_de_memoria_2_output));
  Valor_de_Memoria valor_de_memoria_3 (
    .INPUT(INPUT), .SET(SET), .CLOCK(demultiplexer_1_out2), .RESET(RESET), .OUTPUT(valor_de_memoria_3_output));
  Valor_de_Memoria valor_de_memoria_4 (
    .INPUT(INPUT), .SET(SET), .CLOCK(demultiplexer_1_out3), .RESET(RESET), .OUTPUT(valor_de_memoria_4_output));
  Valor_de_Memoria valor_de_memoria_5 (
    .INPUT(INPUT), .SET(SET), .CLOCK(demultiplexer_1_out4), .RESET(RESET), .OUTPUT(valor_de_memoria_5_output));
  Valor_de_Memoria valor_de_memoria_6 (
    .INPUT(INPUT), .SET(SET), .CLOCK(demultiplexer_1_out5), .RESET(RESET), .OUTPUT(valor_de_memoria_6_output));
  Valor_de_Memoria valor_de_memoria_7 (
    .INPUT(INPUT), .SET(SET), .CLOCK(demultiplexer_1_out6), .RESET(RESET), .OUTPUT(valor_de_memoria_7_output));
  Valor_de_Memoria valor_de_memoria_8 (
    .INPUT(INPUT), .SET(SET), .CLOCK(demultiplexer_1_out7), .RESET(RESET), .OUTPUT(valor_de_memoria_8_output));
  Valor_de_Memoria valor_de_memoria_9 (
    .INPUT(INPUT), .SET(SET), .CLOCK(demultiplexer_1_out8), .RESET(RESET), .OUTPUT(valor_de_memoria_9_output));
  Valor_de_Memoria valor_de_memoria_10 (
    .INPUT(INPUT), .SET(SET), .CLOCK(demultiplexer_1_out9), .RESET(RESET), .OUTPUT(valor_de_memoria_10_output));
  Valor_de_Memoria valor_de_memoria_11 (
    .INPUT(INPUT), .SET(SET), .CLOCK(demultiplexer_1_out10), .RESET(RESET),
    .OUTPUT(valor_de_memoria_11_output));
  Valor_de_Memoria valor_de_memoria_12 (
    .INPUT(INPUT), .SET(SET), .CLOCK(demultiplexer_1_out11), .RESET(RESET),
    .OUTPUT(valor_de_memoria_12_output));
  Valor_de_Memoria valor_de_memoria_13 (
    .INPUT(INPUT), .SET(SET), .CLOCK(demultiplexer_1_out12), .RESET(RESET),
    .OUTPUT(valor_de_memoria_13_output));
  Valor_de_Memoria valor_de_memoria_14 (
    .INPUT(INPUT), .SET(SET), .CLOCK(demultiplexer_1_out13), .RESET(RESET),
    .OUTPUT(valor_de_memoria_14_output));
  Valor_de_Memoria valor_de_memoria_15 (
    .INPUT(INPUT), .SET(SET), .CLOCK(demultiplexer_1_out14), .RESET(RESET),
    .OUTPUT(valor_de_memoria_15_output));
  Valor_de_Memoria valor_de_memoria_16 (
    .INPUT(INPUT), .SET(SET), .CLOCK(demultiplexer_1_out15), .RESET(RESET),
    .OUTPUT(valor_de_memoria_16_output));
  // Probe on valor_de_memoria_1_output
  // Probe on valor_de_memoria_2_output
  // Probe on valor_de_memoria_3_output
  // Probe on valor_de_memoria_4_output
  // Probe on valor_de_memoria_5_output
  // Probe on valor_de_memoria_6_output
  // Probe on valor_de_memoria_7_output
  // Probe on valor_de_memoria_8_output
  // Probe on valor_de_memoria_9_output
  // Probe on valor_de_memoria_10_output
  // Probe on valor_de_memoria_11_output
  // Probe on valor_de_memoria_12_output
  // Probe on valor_de_memoria_13_output
  // Probe on valor_de_memoria_14_output
  // Probe on valor_de_memoria_15_output
  // Probe on valor_de_memoria_16_output
  // Probe on subtractor_1_out
  Multiplexer #(.select(4), .width(8)) multiplexer_2 (
    .in0(valor_de_memoria_1_output), .in1(valor_de_memoria_2_output), .in2(valor_de_memoria_3_output),
    .in3(valor_de_memoria_4_output), .in4(valor_de_memoria_5_output), .in5(valor_de_memoria_6_output),
    .in6(valor_de_memoria_7_output), .in7(valor_de_memoria_8_output), .in8(valor_de_memoria_9_output),
    .in9(valor_de_memoria_10_output), .in10(valor_de_memoria_11_output), .in11(valor_de_memoria_12_output),
    .in12(valor_de_memoria_13_output), .in13(valor_de_memoria_14_output), .in14(valor_de_memoria_15_output),
    .in15(valor_de_memoria_16_output), .out(multiplexer_2_out), .sel(subtractor_1_out));  // open: en
  Multiplexer #(.width(8)) multiplexer_3 (
    .in0({8{1'b0}}), .in1(multiplexer_2_out), .out(OUTPUT), .sel(ESC_0_LER_1));  // open: en
endmodule
