// Logisim project Questão 7 - Banco de Registradores.circ as structural Verilog: 2 circuits, main circuit Banco de Registradores
module Registrador (
  input  [7:0] INPUT,
  input  CLOCK,
  input  SET,
  input  RESET,
  output [7:0] OUTPUT
);

  D_Flip_Flop d_ff_1 (.clk(CLOCK), .D(INPUT[0]), .Q(OUTPUT[0]), .preset(SET), .reset(RESET));  // open: Qn, en
  D_Flip_Flop d_ff_2 (.clk(CLOCK), .D(INPUT[1]), .Q(OUTPUT[1]), .preset(SET), .reset(RESET));  // open: Qn, en
  D_Flip_Flop d_ff_3 (.clk(CLOCK), .D(INPUT[2]), .Q(OUTPUT[2]), .preset(SET), .reset(RESET));  // open: Qn, en
  D_Flip_Flop d_ff_4 (.clk(CLOCK), .D(INPUT[3]), .Q(OUTPUT[3]), .preset(SET), .reset(RESET));  // open: Qn, en
  D_Flip_Flop d_ff_5 (.clk(CLOCK), .D(INPUT[4]), .Q(OUTPUT[4]), .preset(SET), .reset(RESET));  // open: Qn, en
  D_Flip_Flop d_ff_6 (.clk(CLOCK), .D(INPUT[5]), .Q(OUTPUT[5]), .preset(SET), .reset(RESET));  // open: Qn, en
  D_Flip_Flop d_ff_7 (.clk(CLOCK), .D(INPUT[6]), .Q(OUTPUT[6]), .preset(SET), .reset(RESET));  // open: Qn, en
  D_Flip_Flop d_ff_8 (.clk(CLOCK), .D(INPUT[7]), .Q(OUTPUT[7]), .preset(SET), .reset(RESET));  // open: Qn, en
endmodule

module Banco_de_Registradores (
  input  RESET,
  input  [7:0] INPUT,
  input  SET,
  input  [1:0] \ENDEREÇO ,
  output [7:0] out_5,
  output [7:0] out_6,
  output [7:0] out_7,
  output [7:0] out_8
);

  wire CLOCK_out, demultiplexer_1_out0, demultiplexer_1_out1, demultiplexer_1_out2, demultiplexer_1_out3;

  Clock CLOCK (.out(CLOCK_out));
  Demultiplexer #(.select(2)) demultiplexer_1 (
    .out0(demultiplexer_1_out0), .out1(demultiplexer_1_out1), .out2(demultiplexer_1_out2),
    .out3(demultiplexer_1_out3), .in(CLOCK_out), .sel(\ENDEREÇO ));  // open: en
  Registrador registrador_1 (.INPUT(INPUT), .CLOCK(demultiplexer_1_out0), .SET(SET), .RESET(RESET), .OUTPUT(out_5));
  Registrador registrador_2 (.INPUT(INPUT), .CLOCK(demultiplexer_1_out1), .SET(SET), .RESET(RESET), .OUTPUT(out_6));
  Registrador registrador_3 (.INPUT(INPUT), .CLOCK(demultiplexer_1_out2), .SET(SET), .RESET(RESET), .OUTPUT(out_7));
  Registrador registrador_4 (.INPUT(INPUT), .CLOCK(demultiplexer_1_out3), .SET(SET), .RESET(RESET), .OUTPUT(out_8));
endmodule
