// Logisim project Questão 7 - Banco de Registradores.circ.circ as structural Verilog: 2 circuits, main circuit Banco de Registradores
module Registrador (
  input  [7:0] INPUT,
  input  CLOCK,
  input  SET,
  input  RESET,
  output [7:0] OUTPUT
);

  D_Flip_Flop d_ff_1 (.clk(CLOCK), .D(INPUT[0]), .Q(OUTPUT[0]), .preset(SET), .reset(RESET));  // open: Qn, en
  D_Flip_Flop d_ff_2 (.clk(CLOCK), .D(INPUT[1]), .Q(OUTPUT[1]), .preset(SET), .reset(RESET));  // open: Qn, en
  D_Flip_Flop d_ff_3 (.clk(CLOCK), .D(INPUT[2]), .Q(OUTPUT[2]), .preset(SET), .reset(RESET));  // open: Qn, en
  D_Flip_Flop d_ff_4 (.clk(CLOCK), .D(INPUT[3]), .Q(OUTPUT[3]), .preset(SET), .reset(RESET));  // open: Qn, en
  D_Flip_Flop d_ff_5 (.clk(CLOCK), .D(INPUT[4]), .Q(OUTPUT[4]), .preset(SET), .reset(RESET));  // open: Qn, en
  D_Flip_Flop d_ff_6 (.clk(CLOCK), .D(INPUT[5]), .Q(OUTPUT[5]), .preset(SET), .reset(RESET));  // open: Qn, en
  D_Flip_Flop d_ff_7 (.clk(CLOCK), .D(INPUT[6]), .Q(OUTPUT[6]), .preset(SET), .reset(RESET));  // open: Qn, en
  D_Flip_Flop d_ff_8 (.clk(CLOCK), .D(INPUT[7]), .Q(OUTPUT[7]), .preset(SET), .reset(RESET));  // open: Qn, en
endmodule

module Banco_de_Registradores (
  input  ESC_0_LER_1,
  input  RESET,
  input  [7:0] INPUT,
  input  SET,
  input  [1:0] \ENDEREÇO_R1 ,
  input  [1:0] \ENDEREÇO_R2 ,
  output [7:0] R1,
  output [7:0] R2
);

  wire CLOCK_out, demultiplexer_1_out0, demultiplexer_1_out1, demultiplexer_1_out2, demultiplexer_1_out3,
       multiplexer_1_out;
  wire [7:0] multiplexer_3_out, multiplexer_5_out, registrador_2_output, registrador_3_output,
       registrador_4_output, registrador_5_output;

  Clock CLOCK (.out(CLOCK_out));
  Multiplexer multiplexer_1 (.in0(CLOCK_out), .in1(1'b0), .out(multiplexer_1_out), .sel(ESC_0_LER_1));  // open: en
  Demultiplexer #(.select(2)) demultiplexer_1 (
    .out0(demultiplexer_1_out0), .out1(demultiplexer_1_out1), .out2(demultiplexer_1_out2),
    .out3(demultiplexer_1_out3), .in(multiplexer_1_out), .sel(\ENDEREÇO_R1 ));  // open: en
  Registrador registrador_1 ();  // open: INPUT, CLOCK, SET, RESET, OUTPUT
  Registrador registrador_2 (
    .INPUT(INPUT), .CLOCK(demultiplexer_1_out0), .SET(SET), .RESET(RESET), .OUTPUT(registrador_2_output));
  Registrador registrador_3 (
    .INPUT(INPUT), .CLOCK(demultiplexer_1_out1), .SET(SET), .RESET(RESET), .OUTPUT(registrador_3_output));
  Registrador registrador_4 (
    .INPUT(INPUT), .CLOCK(demultiplexer_1_out2), .SET(SET), .RESET(RESET), .OUTPUT(registrador_4_output));
  Registrador registrador_5 (
    .INPUT(INPUT), .CLOCK(demultiplexer_1_out3), .SET(SET), .RESET(RESET), .OUTPUT(registrador_5_output));
  // Probe on registrador_2_output
  // Probe on registrador_3_output
  // Probe on registrador_4_output
  // Probe on registrador_5_output
  Multiplexer #(.width(8)) multiplexer_2 (
    .in0({8{1'b0}}), .in1(multiplexer_3_out), .out(R1), .sel(ESC_0_LER_1));  // open: en
  Multiplexer #(.select(2), .width(8)) multiplexer_3 (
    .in0(registrador_2_output), .in1(registrador_3_output), .in2(registrador_4_output),
    .in3(registrador_5_output), .out(multiplexer_3_out), .sel(\ENDEREÇO_R1 ));  // open: en
  Multiplexer #(.width(8)) multiplexer_4 (
    .in0({8{1'b0}}), .in1(multiplexer_5_out), .out(R2), .sel(ESC_0_LER_1));  // open: en
  Multiplexer #(.select(2), .width(8)) multiplexer_5 (
    .in0(registrador_2_output), .in1(registrador_3_output), .in2(registrador_4_output),
    .in3(registrador_5_output), .out(multiplexer_5_out), .sel(\ENDEREÇO_R2 ));  // open: en
endmodule
