// Logisim project Questão 8 - Somador.circ as structural Verilog: 1 circuit, main circuit main
module main (
  input  in_1,
  input  in_2,
  input  in_3,
  input  in_4,
  input  in_5,
  input  in_6,
  input  in_7,
  input  in_8,
  input  in_9,
  input  in_10,
  input  in_11,
  input  in_12,
  input  in_13,
  input  in_14,
  input  in_15,
  input  in_16,
  output out_17,
  output out_18,
  output out_19,
  output out_20,
  output out_21,
  output out_22,
  output out_23,
  output out_24,
  output out_25
);

  wire and_1_out, and_2_out, and_3_out, and_4_out, and_5_out, and_6_out, and_7_out, and_8_out, and_9_out,
       and_10_out, and_11_out, and_12_out, and_13_out, and_14_out, and_15_out, and_16_out, and_17_out,
       and_18_out, and_19_out, and_20_out, and_21_out, and_22_out, or_1_out, or_2_out, or_3_out, or_4_out,
       or_5_out, or_6_out, xor_1_out, xor_3_out, xor_5_out, xor_7_out, xor_9_out, xor_11_out, xor_13_out,
       xor_15_out;

  xor xor_1 (xor_1_out, in_16, in_8);
  and and_1 (and_1_out, in_16, in_8);
  xor xor_2 (out_25, xor_1_out, 1'b0);
  and and_2 (and_2_out, in_7, in_15);
  and and_3 (and_3_out, in_7, and_1_out);
  and and_4 (and_4_out, in_15, and_1_out);
  xor xor_3 (xor_3_out, in_15, in_7);
  or or_1 (or_1_out, and_2_out, and_3_out, and_4_out);
  xor xor_4 (out_24, xor_3_out, and_1_out);
  and and_5 (and_5_out, in_6, in_14);
  and and_6 (and_6_out, in_6, or_1_out);
  and and_7 (and_7_out, in_14, or_1_out);
  xor xor_5 (xor_5_out, in_14, in_6);
  xor xor_6 (out_23, xor_5_out, or_1_out);
  or or_2 (or_2_out, and_5_out, and_6_out, and_7_out);
  xor xor_7 (xor_7_out, in_13, in_5);
  and and_8 (and_8_out, in_5, in_13);
  and and_9 (and_9_out, in_5, or_2_out);
  and and_10 (and_10_out, in_13, or_2_out);
  or or_3 (or_3_out, and_8_out, and_9_out, and_10_out);
  xor xor_8 (out_22, xor_7_out, or_2_out);
  xor xor_9 (xor_9_out, in_12, in_4);
  and and_11 (and_11_out, in_4, in_12);
  and and_12 (and_12_out, in_4, or_3_out);
  and and_13 (and_13_out, in_12, or_3_out);
  or or_4 (or_4_out, and_11_out, and_12_out, and_13_out);
  xor xor_10 (out_21, xor_9_out, or_3_out);
  and and_14 (and_14_out, in_3, in_11);
  and and_15 (and_15_out, in_3, or_4_out);
  and and_16 (and_16_out, in_11, or_4_out);
  xor xor_11 (xor_11_out, in_11, in_3);
  or or_5 (or_5_out, and_14_out, and_15_out, and_16_out);
  xor xor_12 (out_20, xor_11_out, or_4_out);
  and and_17 (and_17_out, in_2, in_10);
  and and_18 (and_18_out, in_2, or_5_out);
  and and_19 (and_19_out, in_10, or_5_out);
  xor xor_13 (xor_13_out, in_10, in_2);
  or or_6 (or_6_out, and_17_out, and_18_out, and_19_out);
  xor xor_14 (out_19, xor_13_out, or_5_out);
  and and_20 (and_20_out, in_1, in_9);
  and and_21 (and_21_out, in_1, or_6_out);
  and and_22 (and_22_out, in_9, or_6_out);
  xor xor_15 (xor_15_out, in_9, in_1);
  or or_7 (out_17, and_20_out, and_21_out, and_22_out);
  xor xor_16 (out_18, xor_15_out, or_6_out);
endmodule
