// Logisim project Questão 9 - Unidade de Controle MIPS.circ as structural Verilog: 2 circuits, main circuit FF JK
module Controle_MIPS_16bits (
  input  [5:0] in_1,
  input  in_2,
  input  in_3,
  output RegDST,
  output OrigALU,
  output MemParaReg,
  output EscReg,
  output LeMem,
  output EscMem,
  output AluOp1,
  output AluOp0,
  output RESET,
  output AtualPc
);

  wire and_1_out, and_2_out, and_3_out, and_4_out, and_5_out, clock_1_out, demultiplexer_1_out2,
       demultiplexer_1_out4, demultiplexer_2_out1, demultiplexer_2_out5, demultiplexer_3_out1,
       demultiplexer_3_out3, ff_jk_1_q, not_1_out, not_2_out, not_3_out, not_4_out, not_5_out, not_6_out,
       not_7_out, not_8_out, not_9_out, not_10_out, not_11_out, ON_OFF_out, or_1_out, or_2_out;
  wire [2:0] counter_1_q;

  not not_1 (not_1_out, in_1[0]);
  not not_2 (not_2_out, in_1[1]);
  not not_3 (not_3_out, in_1[2]);
  not not_4 (not_4_out, in_1[3]);
  not not_5 (not_5_out, in_1[4]);
  not not_6 (not_6_out, in_1[5]);
  not not_7 (not_7_out, in_1[1]);
  not not_8 (not_8_out, in_1[2]);
  not not_9 (not_9_out, in_1[3]);
  not not_10 (not_10_out, in_1[1]);
  not not_11 (not_11_out, in_1[3]);
  Button ON_OFF (.out(ON_OFF_out));
  and and_1 (and_1_out, not_1_out, not_2_out, not_3_out, not_4_out, not_5_out, not_6_out);
  and and_2 (and_2_out, in_1[0], not_7_out, not_8_out, not_9_out, in_1[4], in_1[5]);
  and and_3 (and_3_out, in_1[0], not_10_out, in_1[2], not_11_out, in_1[4], in_1[5]);
  and and_4 (and_4_out, in_1[0], in_1[1], in_1[2], in_1[3], in_1[4], in_1[5]);
  or or_1 (or_1_out, and_1_out, and_2_out, and_3_out);
  Clock clock_1 (.out(clock_1_out));
  FF_JK ff_jk_1 (.J(1'b1), .CLOCK(or_2_out), .K(1'b1), .SET(in_2), .RESET(in_3), .Q(ff_jk_1_q));  // open: nQ
  or or_2 (or_2_out, and_4_out, ON_OFF_out);
  Counter #(.width(3), .max('h7)) counter_1 (
    .count(or_1_out), .Q(counter_1_q), .clk(and_5_out), .clr(RESET));  // open: load, D, carry
  not not_12 (RESET, ff_jk_1_q);
  and and_5 (and_5_out, clock_1_out, ff_jk_1_q);
  Demultiplexer #(.select(3)) demultiplexer_1 (
    .out1(RegDST), .out2(demultiplexer_1_out2), .out3(AluOp1), .out4(demultiplexer_1_out4), .in(and_1_out),
    .sel(counter_1_q));  // open: out0, out5, out6, out7, en
  Demultiplexer #(.select(3)) demultiplexer_2 (
    .out1(demultiplexer_2_out1), .out2(LeMem), .out3(MemParaReg), .out4(EscReg), .out5(demultiplexer_2_out5),
    .in(and_2_out), .sel(counter_1_q));  // open: out0, out6, out7, en
  Demultiplexer #(.select(3)) demultiplexer_3 (
    .out1(demultiplexer_3_out1), .out2(EscMem), .out3(demultiplexer_3_out3), .in(and_3_out), .sel(counter_1_q));  // open: out0, out4, out5, out6, out7, en
  or or_3 (OrigALU, demultiplexer_1_out2, demultiplexer_2_out1, demultiplexer_3_out1);
  or or_4 (AtualPc, demultiplexer_1_out4, demultiplexer_2_out5, demultiplexer_3_out3);

  assign AluOp0 = 1'b0;

  // Notes on the sheet:
  //   R
  //   LW
  //   SW
endmodule

module FF_JK (
  input  SET,
  input  J,
  input  CLOCK,
  input  K,
  input  RESET,
  output Q,
  output nQ
);

  wire nand_1_out, nand_2_out, nand_3_out, nand_4_out, nand_5_out, nand_6_out, not_1_out, not_2_out,
       not_3_out, not_4_out;

  not not_1 (not_1_out, CLOCK);
  not not_2 (not_2_out, SET);
  nand nand_1 (nand_1_out, nQ, J, not_1_out);
  nand nand_2 (nand_2_out, not_1_out, K, Q);
  not not_3 (not_3_out, RESET);
  nand nand_3 (nand_3_out, not_2_out, nand_1_out, nand_4_out);
  not not_4 (not_4_out, not_1_out);
  nand nand_4 (nand_4_out, nand_3_out, nand_2_out, not_3_out);
  nand nand_5 (nand_5_out, nand_3_out, not_3_out, not_4_out);
  nand nand_6 (nand_6_out, not_4_out, not_2_out, nand_4_out);
  nand nand_7 (Q, not_2_out, nQ, nand_5_out);
  nand nand_8 (nQ, nand_6_out, Q, not_3_out);
endmodule
